# Fritzing sketch buggy project (saved by Fritzing 0.8.7b)
breadboards: 1

parts:
  Part1 = Arduino Mega 2560 (Rev3)
  Part2 = Arduino Motor Shield (Rev3)
  M1 = DC Motor
  M2 = DC Motor
  LCD1 = LCD screen
  LCM1602_IIC1 = LCM1602 IIC [part_number="LCM1602 IIC" chip_label="LCM1602 IIC" package="DIP (Dual Inline) [THT]"]
  U1 = ESP32-38PinWide [part_number=ESP32-38PinWide]
  Part3 = SRF05 Ultrasonic Rangefinder

nets:
  N1: Part1.D21/SCL, LCM1602_IIC1.SCL
  N2: Part1.D20/SDA, LCM1602_IIC1.SDA
  VCC: Part1.5V, LCM1602_IIC1.VCC, Part3.VCC
  N3: Part1.D40, Part3.Trig
  N4: Part1.D41, Part3.Echo
  GND: Part1.GND, LCM1602_IIC1.GND, Part3.GND
  N5: Part2.IOREF, U1.GPIO1
  N6: Part2.D1/TX, U1.GPIO3
  N7: Part2.D2, U1.GPIO18
  N8: Part2.B-, M1.pin_2
  N9: Part2.B+, M1.pin_1
  N10: Part2.A-, M2.pin_2
  N11: Part2.A+, M2.pin_1
  N12: Part2.3V3, U1.3.3
  GND_2: Part2.GND, U1.GND
  VSS: LCD1.VSS, LCM1602_IIC1.VSS
  VDD: LCD1.VDD, LCM1602_IIC1.VDD
  N13: LCD1.V0, LCM1602_IIC1.V0
  N14: LCD1.RS, LCM1602_IIC1.RS
  N15: LCD1.R/W, LCM1602_IIC1.RW
  N16: LCD1.E, LCM1602_IIC1.E
  N17: LCD1.DB0, LCM1602_IIC1.D0
  N18: LCD1.DB1, LCM1602_IIC1.D1
  N19: LCD1.DB2, LCM1602_IIC1.D2
  N20: LCD1.DB3, LCM1602_IIC1.D3
  N21: LCD1.DB4, LCM1602_IIC1.D4
  N22: LCD1.DB5, LCM1602_IIC1.D5
  N23: LCD1.DB6, LCM1602_IIC1.D6
  N24: LCD1.DB7, LCM1602_IIC1.D7
  N25: LCD1.LED+, LCM1602_IIC1.A
  N26: LCD1.LED-, LCM1602_IIC1.K
  N27: LCM1602_IIC1.LED_A, LCM1602_IIC1.LED_B

custom parts:
  LCM1602 IIC: I2C-Module to use a 1602 or 2004 LCD on with the wire.h libory Serial LCD Modul
  ESP32-38PinWide: Generic 38-Pin ESP32 with wide format (only access to one side of pins on a breadboard) based on Stephen Lilley's HiLetgo ESP-WROOM-32 ESP32 ESP-32S Development Board.
